// Logisim project lab06.circ as structural Verilog: 4 circuits, main circuit main
module main (
  input  in_1,
  input  in_2
);
endmodule

module One_bit_Adder (
  input  A,
  input  Cin,
  input  B,
  output Result,
  output Result_2
);

  wire and_1_out, and_2_out, and_3_out, and_4_out, and_5_out, and_6_out, and_7_out, and_8_out, and_9_out,
       and_10_out, and_11_out, not_1_out, not_2_out, not_3_out, or_1_out, or_2_out, or_3_out;

  not not_1 (not_1_out, A);
  not not_2 (not_2_out, B);
  not not_3 (not_3_out, Cin);
  and and_1 (and_1_out, not_1_out, not_2_out);
  and and_2 (and_2_out, not_1_out, B);
  and and_3 (and_3_out, A, not_2_out);
  and and_4 (and_4_out, A, B);
  and and_5 (and_5_out, and_1_out, Cin);
  and and_6 (and_6_out, and_2_out, not_3_out);
  and and_7 (and_7_out, and_3_out, not_3_out);
  and and_8 (and_8_out, and_4_out, Cin);
  and and_9 (and_9_out, A, B);
  and and_10 (and_10_out, A, Cin);
  and and_11 (and_11_out, B, Cin);
  or or_1 (or_1_out, and_5_out, and_6_out);
  or or_2 (or_2_out, and_7_out, and_8_out);
  or or_3 (or_3_out, and_9_out, and_10_out);
  or or_4 (Result, or_1_out, or_2_out);
  or or_5 (Result_2, or_3_out, and_11_out);
endmodule

module Four_bit_Adder (
  input  [3:0] A,
  input  [3:0] B,
  input  [3:0] Result
);

  wire one_bit_adder_1_result_2, one_bit_adder_2_result_2, one_bit_adder_3_result_2;

  One_bit_Adder one_bit_adder_1 (
    .A(A[0]), .B(B[0]), .Cin(1'b0), .Result_2(one_bit_adder_1_result_2), .Result(Result[0]));
  One_bit_Adder one_bit_adder_2 (
    .A(A[1]), .B(B[1]), .Cin(one_bit_adder_1_result_2), .Result_2(one_bit_adder_2_result_2),
    .Result(Result[1]));
  One_bit_Adder one_bit_adder_3 (
    .A(A[2]), .B(B[2]), .Cin(one_bit_adder_2_result_2), .Result_2(one_bit_adder_3_result_2),
    .Result(Result[2]));
  One_bit_Adder one_bit_adder_4 (
    .A(A[3]), .B(B[3]), .Cin(one_bit_adder_3_result_2), .Result(Result[3]));  // open: Result_2
endmodule

module Eight_Bit (
  input  [7:0] Adder_Probe,
  input  [7:0] A,
  input  [7:0] B,
  input  [7:0] Result,
  input  [7:0] Subtractor_probe,
  input  Operation
);

  Adder adder_1 (.a(A), .b(B), .out(Adder_Probe), .cin(1'b0));  // open: cout
  Subtractor subtractor_1 (.a(A), .b(B), .out(Subtractor_probe), .bin(1'b0));  // open: bout
  Multiplexer #(.width(8)) multiplexer_1 (
    .in0(Adder_Probe), .in1(Subtractor_probe), .out(Result), .en(Operation));  // open: sel
endmodule
