// Logisim project lab08.circ as structural Verilog: 3 circuits, main circuit main
module main (
  input  Ainvert,
  input  Binvert,
  input  CarryIn,
  input  [1:0] Operation,
  input  A,
  input  B,
  input  Less,
  output Result,
  output Set,
  output CarryOut,
  output OverFlow
);

  wire and_1_out, multiplexer_1_out, multiplexer_2_out, not_1_out, not_2_out, or_1_out;

  not not_1 (not_1_out, A);
  Multiplexer multiplexer_1 (.in0(A), .in1(not_1_out), .out(multiplexer_1_out), .sel(Ainvert));  // open: en
  not not_2 (not_2_out, B);
  Multiplexer multiplexer_2 (.in0(B), .in1(not_2_out), .out(multiplexer_2_out), .sel(Binvert));  // open: en
  xor xor_1 (OverFlow, CarryOut, CarryIn);
  and and_1 (and_1_out, multiplexer_1_out, multiplexer_2_out);
  or or_1 (or_1_out, multiplexer_1_out, multiplexer_2_out);
  Adder #(.width(1)) adder_1 (.a(multiplexer_1_out), .b(multiplexer_2_out), .out(Set), .cin(CarryIn), .cout(CarryOut));
  Multiplexer #(.select(2)) multiplexer_3 (
    .in0(and_1_out), .in1(or_1_out), .in2(Set), .in3(Less), .out(Result), .sel(Operation));  // open: en
endmodule

module ALU (
  input  [3:0] Ainvert_Bnegate_op,
  input  [7:0] A,
  input  [7:0] B,
  output Zero,
  output [7:0] Result,
  output Overflow
);

  wire main_1_carryout, main_2_carryout, main_3_carryout, main_4_carryout, main_5_carryout, main_6_carryout,
       main_7_carryout, main_8_set, or_1_out;

  main main_1 (
    .A(A[0]), .B(B[0]), .Less(main_8_set), .Ainvert(Ainvert_Bnegate_op[3]), .Binvert(Ainvert_Bnegate_op[2]),
    .CarryIn(Ainvert_Bnegate_op[2]), .Operation(Ainvert_Bnegate_op[1:0]), .CarryOut(main_1_carryout),
    .Result(Result[0]));  // open: Set, OverFlow
  main main_2 (
    .A(A[1]), .B(B[1]), .Less(1'b0), .Ainvert(Ainvert_Bnegate_op[3]), .Binvert(Ainvert_Bnegate_op[2]),
    .CarryIn(main_1_carryout), .Operation(Ainvert_Bnegate_op[1:0]), .CarryOut(main_2_carryout),
    .Result(Result[1]));  // open: Set, OverFlow
  main main_3 (
    .A(A[2]), .B(B[2]), .Less(1'b0), .Ainvert(Ainvert_Bnegate_op[3]), .Binvert(Ainvert_Bnegate_op[2]),
    .CarryIn(main_2_carryout), .Operation(Ainvert_Bnegate_op[1:0]), .CarryOut(main_3_carryout),
    .Result(Result[2]));  // open: Set, OverFlow
  main main_4 (
    .A(A[3]), .B(B[3]), .Less(1'b0), .Ainvert(Ainvert_Bnegate_op[3]), .Binvert(Ainvert_Bnegate_op[2]),
    .CarryIn(main_3_carryout), .Operation(Ainvert_Bnegate_op[1:0]), .CarryOut(main_4_carryout),
    .Result(Result[3]));  // open: Set, OverFlow
  main main_5 (
    .A(A[4]), .B(B[4]), .Less(1'b0), .Ainvert(Ainvert_Bnegate_op[3]), .Binvert(Ainvert_Bnegate_op[2]),
    .CarryIn(main_4_carryout), .Operation(Ainvert_Bnegate_op[1:0]), .CarryOut(main_5_carryout),
    .Result(Result[4]));  // open: Set, OverFlow
  main main_6 (
    .A(A[5]), .B(B[5]), .Less(1'b0), .Ainvert(Ainvert_Bnegate_op[3]), .Binvert(Ainvert_Bnegate_op[2]),
    .CarryIn(main_5_carryout), .Operation(Ainvert_Bnegate_op[1:0]), .CarryOut(main_6_carryout),
    .Result(Result[5]));  // open: Set, OverFlow
  main main_7 (
    .A(A[6]), .B(B[6]), .Less(1'b0), .Ainvert(Ainvert_Bnegate_op[3]), .Binvert(Ainvert_Bnegate_op[2]),
    .CarryIn(main_6_carryout), .Operation(Ainvert_Bnegate_op[1:0]), .CarryOut(main_7_carryout),
    .Result(Result[6]));  // open: Set, OverFlow
  main main_8 (
    .A(A[7]), .B(B[7]), .Less(1'b0), .Ainvert(Ainvert_Bnegate_op[3]), .Binvert(Ainvert_Bnegate_op[2]),
    .CarryIn(main_7_carryout), .Operation(Ainvert_Bnegate_op[1:0]), .Result(Result[7]), .Set(main_8_set),
    .OverFlow(Overflow));  // open: CarryOut
  not not_1 (Zero, or_1_out);
  or or_1 (or_1_out, Result[0], Result[1], Result[2], Result[3], Result[4], Result[5], Result[6], Result[7]);
endmodule

module main_circuit (
  input  [3:0] Operation,
  input  [7:0] A,
  input  [7:0] B,
  output Zero,
  output [7:0] Result,
  output Overflow
);

  ALU alu_1 (.A(A), .B(B), .Ainvert_Bnegate_op(Operation), .Zero(Zero), .Result(Result), .Overflow(Overflow));
endmodule
