// Logisim project lab09.circ as structural Verilog: 7 circuits, main circuit final
module main (
  input  [2:0] Read_Register_1,
  input  [2:0] Write_Register,
  input  [2:0] Read_register_2,
  input  Write,
  input  [31:0] Data,
  input  Clock,
  output [31:0] Read_data_1,
  output [31:0] Read_data_2
);

  wire [31:0] Register_0_q, Register_1_q, Register_2_q, Register_3_q, Register_4_q, Register_5_q,
       Register_6_q, Register_7_q, write_1_register_0, write_1_register_1, write_1_register_2,
       write_1_register_3, write_1_register_4, write_1_register_5, write_1_register_6, write_1_register_7;

  write write_1 (
    .Write(Write), .Register_number(Write_Register), .Register_Data(Data), .in_4(Clock),
    .Register_0(write_1_register_0), .Register_1(write_1_register_1), .Register_2(write_1_register_2),
    .Register_3(write_1_register_3), .Register_4(write_1_register_4), .Register_5(write_1_register_5),
    .Register_6(write_1_register_6), .Register_7(write_1_register_7));
  Register #(.width(32), .trigger("falling")) Register_0 (
    .D(write_1_register_0), .Q(Register_0_q), .clk(Clock));  // open: en, clr
  Register #(.width(32), .trigger("falling")) Register_1 (
    .D(write_1_register_1), .Q(Register_1_q), .clk(Clock));  // open: en, clr
  Register #(.width(32), .trigger("falling")) Register_2 (
    .D(write_1_register_2), .Q(Register_2_q), .clk(Clock));  // open: en, clr
  Register #(.width(32), .trigger("falling")) Register_3 (
    .D(write_1_register_3), .Q(Register_3_q), .clk(Clock));  // open: en, clr
  Register #(.width(32), .trigger("falling")) Register_4 (
    .D(write_1_register_4), .Q(Register_4_q), .clk(Clock));  // open: en, clr
  Register #(.width(32), .trigger("falling")) Register_5 (
    .D(write_1_register_5), .Q(Register_5_q), .clk(Clock));  // open: en, clr
  Register #(.width(32), .trigger("falling")) Register_6 (
    .D(write_1_register_6), .Q(Register_6_q), .clk(Clock));  // open: en, clr
  Register #(.width(32), .trigger("falling")) Register_7 (
    .D(write_1_register_7), .Q(Register_7_q), .clk(Clock));  // open: en, clr
  Multiplexer #(.select(3), .width(32)) multiplexer_1 (
    .in0(Register_0_q), .in1(Register_1_q), .in2(Register_2_q), .in3(Register_3_q), .in4(Register_4_q),
    .in5(Register_5_q), .in6(Register_6_q), .in7(Register_7_q), .out(Read_data_1), .sel(Read_Register_1));  // open: en
  Multiplexer #(.select(3), .width(32)) multiplexer_2 (
    .in0(Register_0_q), .in1(Register_1_q), .in2(Register_2_q), .in3(Register_3_q), .in4(Register_4_q),
    .in5(Register_5_q), .in6(Register_6_q), .in7(Register_7_q), .out(Read_data_2), .sel(Read_register_2));  // open: en
endmodule

module write (
  input  Write,
  input  [2:0] Register_number,
  input  [31:0] Register_Data,
  input  in_4,
  output [31:0] Register_0,
  output [31:0] Register_1,
  output [31:0] Register_2,
  output [31:0] Register_3,
  output [31:0] Register_4,
  output [31:0] Register_5,
  output [31:0] Register_6,
  output [31:0] Register_7
);

  wire and_1_out, and_2_out, and_3_out, and_4_out, and_5_out, and_6_out, and_7_out, and_8_out,
       decoder_1_out0, decoder_1_out1, decoder_1_out2, decoder_1_out3, decoder_1_out4, decoder_1_out5,
       decoder_1_out6, decoder_1_out7;

  Decoder #(.select(3)) decoder_1 (
    .out0(decoder_1_out0), .out1(decoder_1_out1), .out2(decoder_1_out2), .out3(decoder_1_out3),
    .out4(decoder_1_out4), .out5(decoder_1_out5), .out6(decoder_1_out6), .out7(decoder_1_out7),
    .sel(Register_number));  // open: en
  and and_1 (and_1_out, Write, decoder_1_out0);
  and and_2 (and_2_out, Write, decoder_1_out1);
  and and_3 (and_3_out, Write, decoder_1_out2);
  and and_4 (and_4_out, Write, decoder_1_out3);
  and and_5 (and_5_out, Write, decoder_1_out4);
  and and_6 (and_6_out, Write, decoder_1_out5);
  and and_7 (and_7_out, Write, decoder_1_out6);
  and and_8 (and_8_out, Write, decoder_1_out7);
  _32_bit_d_flip_flop u_32_bit_d_flip_flop_1 (
    .Write_Data(Register_Data), .Enable(and_1_out), .in_3(in_4), .out_4(Register_0));
  _32_bit_d_flip_flop u_32_bit_d_flip_flop_2 (
    .Write_Data(Register_Data), .Enable(and_2_out), .in_3(in_4), .out_4(Register_1));
  _32_bit_d_flip_flop u_32_bit_d_flip_flop_3 (
    .Write_Data(Register_Data), .Enable(and_3_out), .in_3(in_4), .out_4(Register_2));
  _32_bit_d_flip_flop u_32_bit_d_flip_flop_4 (
    .Write_Data(Register_Data), .Enable(and_4_out), .in_3(in_4), .out_4(Register_3));
  _32_bit_d_flip_flop u_32_bit_d_flip_flop_5 (
    .Write_Data(Register_Data), .Enable(and_5_out), .in_3(in_4), .out_4(Register_4));
  _32_bit_d_flip_flop u_32_bit_d_flip_flop_6 (
    .Write_Data(Register_Data), .Enable(and_6_out), .in_3(in_4), .out_4(Register_5));
  _32_bit_d_flip_flop u_32_bit_d_flip_flop_7 (
    .Write_Data(Register_Data), .Enable(and_7_out), .in_3(in_4), .out_4(Register_6));
  _32_bit_d_flip_flop u_32_bit_d_flip_flop_8 (
    .Write_Data(Register_Data), .Enable(and_8_out), .in_3(in_4), .out_4(Register_7));
endmodule

module D_latch (
  input  C,
  input  D,
  output Q,
  output Not_Q
);

  wire and_1_out, and_2_out, not_1_out;

  not not_1 (not_1_out, D);
  and and_1 (and_1_out, C, not_1_out);
  and and_2 (and_2_out, C, D);
  nor nor_1 (Q, and_1_out, Not_Q);
  nor nor_2 (Not_Q, Q, and_2_out);
endmodule

module D_Flip_Flop (
  input  D,
  input  in_2,
  output Q,
  output Not_Q
);

  wire d_latch_1_q, not_1_out;

  not not_1 (not_1_out, in_2);
  D_latch d_latch_1 (.C(in_2), .D(D), .Q(d_latch_1_q));  // open: Not_Q
  D_latch d_latch_2 (.C(not_1_out), .D(d_latch_1_q), .Q(Q), .Not_Q(Not_Q));
endmodule

module _32_bit_d_flip_flop (
  input  [31:0] Write_Data,
  input  Enable,
  input  in_3,
  output [31:0] out_4
);

  wire and_1_out;

  and and_1 (and_1_out, Enable, in_3);
  D_Flip_Flop d_flip_flop_1 (.D(Write_Data[0]), .in_2(and_1_out), .Q(out_4[0]));  // open: Not_Q
  D_Flip_Flop d_flip_flop_2 (.D(Write_Data[1]), .in_2(and_1_out), .Q(out_4[1]));  // open: Not_Q
  D_Flip_Flop d_flip_flop_3 (.D(Write_Data[2]), .in_2(and_1_out), .Q(out_4[2]));  // open: Not_Q
  D_Flip_Flop d_flip_flop_4 (.D(Write_Data[3]), .in_2(and_1_out), .Q(out_4[3]));  // open: Not_Q
  D_Flip_Flop d_flip_flop_5 (.D(Write_Data[4]), .in_2(and_1_out), .Q(out_4[4]));  // open: Not_Q
  D_Flip_Flop d_flip_flop_6 (.D(Write_Data[5]), .in_2(and_1_out), .Q(out_4[5]));  // open: Not_Q
  D_Flip_Flop d_flip_flop_7 (.D(Write_Data[6]), .in_2(and_1_out), .Q(out_4[6]));  // open: Not_Q
  D_Flip_Flop d_flip_flop_8 (.D(Write_Data[7]), .in_2(and_1_out), .Q(out_4[7]));  // open: Not_Q
  D_Flip_Flop d_flip_flop_9 (.D(Write_Data[8]), .in_2(and_1_out), .Q(out_4[8]));  // open: Not_Q
  D_Flip_Flop d_flip_flop_10 (.D(Write_Data[9]), .in_2(and_1_out), .Q(out_4[9]));  // open: Not_Q
  D_Flip_Flop d_flip_flop_11 (.D(Write_Data[10]), .in_2(and_1_out), .Q(out_4[10]));  // open: Not_Q
  D_Flip_Flop d_flip_flop_12 (.D(Write_Data[11]), .in_2(and_1_out), .Q(out_4[11]));  // open: Not_Q
  D_Flip_Flop d_flip_flop_13 (.D(Write_Data[12]), .in_2(and_1_out), .Q(out_4[12]));  // open: Not_Q
  D_Flip_Flop d_flip_flop_14 (.D(Write_Data[13]), .in_2(and_1_out), .Q(out_4[13]));  // open: Not_Q
  D_Flip_Flop d_flip_flop_15 (.D(Write_Data[14]), .in_2(and_1_out), .Q(out_4[14]));  // open: Not_Q
  D_Flip_Flop d_flip_flop_16 (.D(Write_Data[15]), .in_2(and_1_out), .Q(out_4[15]));  // open: Not_Q
  D_Flip_Flop d_flip_flop_17 (.D(Write_Data[16]), .in_2(and_1_out), .Q(out_4[16]));  // open: Not_Q
  D_Flip_Flop d_flip_flop_18 (.D(Write_Data[17]), .in_2(and_1_out), .Q(out_4[17]));  // open: Not_Q
  D_Flip_Flop d_flip_flop_19 (.D(Write_Data[18]), .in_2(and_1_out), .Q(out_4[18]));  // open: Not_Q
  D_Flip_Flop d_flip_flop_20 (.D(Write_Data[19]), .in_2(and_1_out), .Q(out_4[19]));  // open: Not_Q
  D_Flip_Flop d_flip_flop_21 (.D(Write_Data[20]), .in_2(and_1_out), .Q(out_4[20]));  // open: Not_Q
  D_Flip_Flop d_flip_flop_22 (.D(Write_Data[21]), .in_2(and_1_out), .Q(out_4[21]));  // open: Not_Q
  D_Flip_Flop d_flip_flop_23 (.D(Write_Data[22]), .in_2(and_1_out), .Q(out_4[22]));  // open: Not_Q
  D_Flip_Flop d_flip_flop_24 (.D(Write_Data[23]), .in_2(and_1_out), .Q(out_4[23]));  // open: Not_Q
  D_Flip_Flop d_flip_flop_25 (.D(Write_Data[24]), .in_2(and_1_out), .Q(out_4[24]));  // open: Not_Q
  D_Flip_Flop d_flip_flop_26 (.D(Write_Data[25]), .in_2(and_1_out), .Q(out_4[25]));  // open: Not_Q
  D_Flip_Flop d_flip_flop_27 (.D(Write_Data[26]), .in_2(and_1_out), .Q(out_4[26]));  // open: Not_Q
  D_Flip_Flop d_flip_flop_28 (.D(Write_Data[27]), .in_2(and_1_out), .Q(out_4[27]));  // open: Not_Q
  D_Flip_Flop d_flip_flop_29 (.D(Write_Data[28]), .in_2(and_1_out), .Q(out_4[28]));  // open: Not_Q
  D_Flip_Flop d_flip_flop_30 (.D(Write_Data[29]), .in_2(and_1_out), .Q(out_4[29]));  // open: Not_Q
  D_Flip_Flop d_flip_flop_31 (.D(Write_Data[30]), .in_2(and_1_out), .Q(out_4[30]));  // open: Not_Q
  D_Flip_Flop d_flip_flop_32 (.D(Write_Data[31]), .in_2(and_1_out), .Q(out_4[31]));  // open: Not_Q
endmodule

module temp (
);

  write write_1 ();  // open: Write, Register_number, Register_Data, in_4, Register_0, Register_1, Register_2, Register_3, Register_4, Register_5, Register_6, Register_7
endmodule

module \final  (
  input  [2:0] Register_Write,
  input  [2:0] Read_Register_1,
  input  [2:0] Read_Register_2,
  input  Write,
  input  [31:0] Data,
  output [31:0] Read_data_1,
  output [31:0] Read_data_2
);

  wire Clock_out;

  main main_1 (
    .Read_Register_1(Read_Register_1), .Read_register_2(Read_Register_2), .Write(Write),
    .Write_Register(Register_Write), .Data(Data), .Clock(Clock_out), .Read_data_1(Read_data_1),
    .Read_data_2(Read_data_2));
  Clock Clock (.out(Clock_out));
endmodule
