// Logisim project lab10.circ as structural Verilog: 4 circuits, main circuit main
module main (
  output [7:0] A,
  output [7:0] B
);

  wire and_1_out, and_2_out, clock_1_out, decoder_1_dstmux, fields_1_register, not_1_out;
  wire [1:0] decoder_1_alu;
  wire [3:0] fields_1_opcode;
  wire [7:0] adder_1_out, alu_1_output, fields_1_immediate, multiplexer_1_out, PC_q;
  wire [15:0] rom_1_data;

  Adder adder_1 (.a(8'h1), .b(PC_q), .out(adder_1_out));  // open: cin, cout
  Register PC (.D(adder_1_out), .en(1'b1), .Q(PC_q), .clk(clock_1_out));  // open: clr
  Decoder decoder_1 (.Opcode(fields_1_opcode), .ALU(decoder_1_alu), .DstMux(decoder_1_dstmux));
  Multiplexer #(.width(8)) multiplexer_1 (
    .in0(alu_1_output), .in1(fields_1_immediate), .out(multiplexer_1_out), .sel(decoder_1_dstmux));  // open: en
  Fields fields_1 (
    .\input (rom_1_data), .opcode(fields_1_opcode), .Register(fields_1_register),
    .immediate(fields_1_immediate));
  ROM #(.dataWidth(16)) rom_1 (.addr(PC_q), .data(rom_1_data), .sel(1'b1));
  and and_1 (and_1_out, 1'b1, not_1_out);
  not not_1 (not_1_out, fields_1_register);
  and and_2 (and_2_out, 1'b1, fields_1_register);
  ALU alu_1 (.A(A), .B(B), .Output(alu_1_output), .Operation(decoder_1_alu));
  Clock clock_1 (.out(clock_1_out));
  Register register_1 (.D(multiplexer_1_out), .en(and_1_out), .Q(A), .clk(clock_1_out));  // open: clr
  Register register_2 (.D(multiplexer_1_out), .en(and_2_out), .Q(B), .clk(clock_1_out));  // open: clr

  // Notes on the sheet:
  //   Rom
  //   SetMux
  //   contents of rom_1 (hex, n*v repeats v):
  //   1 802 2000 3000 2800 3800 4000 5000
endmodule

module ALU (
  input  [1:0] Operation,
  input  [7:0] A,
  input  [7:0] B,
  output [7:0] Output
);

  wire [7:0] adder_1_out, adder_2_out, and_1_out, not_1_out, or_1_out;

  assign not_1_out = ~B;  // NOT_Gate not_1, 8 bits wide
  assign and_1_out = A & B;  // AND_Gate and_1, 8 bits wide
  assign or_1_out = A | B;  // OR_Gate or_1, 8 bits wide
  Adder adder_1 (.a(A), .b(not_1_out), .out(adder_1_out), .cin(1'b1));  // open: cout
  Adder adder_2 (.a(A), .b(B), .out(adder_2_out));  // open: cin, cout
  Multiplexer #(.select(2), .width(8)) multiplexer_1 (
    .in0(adder_2_out), .in1(adder_1_out), .in2(or_1_out), .in3(and_1_out), .out(Output), .sel(Operation));  // open: en
endmodule

module Fields (
  input  [15:0] \input ,
  output [3:0] opcode,
  output Register,
  output [7:0] immediate
);


  assign immediate = \input [7:0];
  assign opcode = \input [15:12];
  assign Register = \input [11];
endmodule

module Decoder (
  input  [3:0] Opcode,
  output [1:0] ALU,
  output DstMux
);

  wire not_2_out, not_3_out;

  not not_1 (ALU[1], Opcode[1]);
  not not_2 (not_2_out, Opcode[2]);
  and and_1 (DstMux, not_2_out, not_3_out);
  not not_3 (not_3_out, Opcode[1]);

  assign ALU[0] = Opcode[0];
endmodule
