// Logisim project project4_div_sqrt.circ as structural Verilog: 14 circuits, main circuit main
module main (
  input  [15:0] A,
  input  [15:0] B,
  input  example_instruction,
  input  division_instruction,
  input  square_root_instruction,
  output Example_Ready,
  output Division_Ready,
  output Square_Root_Ready
);

  wire clock_1_out, q8_8_to_decimal_1_decimal_point, q8_8_to_decimal_2_decimal_point,
       q8_8_to_decimal_3_decimal_point, q8_8_to_decimal_4_decimal_point, q8_8_to_decimal_5_decimal_point;
  wire [3:0] q8_8_to_decimal_1_bcd1, q8_8_to_decimal_1_bcd1_2, q8_8_to_decimal_1_bcd1_3,
       q8_8_to_decimal_1_bcd1_4, q8_8_to_decimal_1_bcd1_5, q8_8_to_decimal_1_bcd1_6, q8_8_to_decimal_1_bcd2,
       q8_8_to_decimal_2_bcd1, q8_8_to_decimal_2_bcd1_2, q8_8_to_decimal_2_bcd1_3, q8_8_to_decimal_2_bcd1_4,
       q8_8_to_decimal_2_bcd1_5, q8_8_to_decimal_2_bcd1_6, q8_8_to_decimal_2_bcd2, q8_8_to_decimal_3_bcd1,
       q8_8_to_decimal_3_bcd1_2, q8_8_to_decimal_3_bcd1_3, q8_8_to_decimal_3_bcd1_4,
       q8_8_to_decimal_3_bcd1_5, q8_8_to_decimal_3_bcd1_6, q8_8_to_decimal_3_bcd2, q8_8_to_decimal_4_bcd1,
       q8_8_to_decimal_4_bcd1_2, q8_8_to_decimal_4_bcd1_3, q8_8_to_decimal_4_bcd1_4,
       q8_8_to_decimal_4_bcd1_5, q8_8_to_decimal_4_bcd1_6, q8_8_to_decimal_4_bcd2, q8_8_to_decimal_5_bcd1,
       q8_8_to_decimal_5_bcd1_2, q8_8_to_decimal_5_bcd1_3, q8_8_to_decimal_5_bcd1_4,
       q8_8_to_decimal_5_bcd1_5, q8_8_to_decimal_5_bcd1_6, q8_8_to_decimal_5_bcd2;
  wire [15:0] division_1_quotient, example_1_result, square_root_1_solution;

  Hex_Digit_Display hex_digit_display_1 (.value(q8_8_to_decimal_1_bcd2));  // open: dp
  Hex_Digit_Display hex_digit_display_2 (.value(q8_8_to_decimal_2_bcd2));  // open: dp
  Hex_Digit_Display hex_digit_display_3 (.value(q8_8_to_decimal_1_bcd1_2), .dp(q8_8_to_decimal_1_decimal_point));
  Hex_Digit_Display hex_digit_display_4 (.value(q8_8_to_decimal_1_bcd1));  // open: dp
  Q8_8_to_Decimal q8_8_to_decimal_1 (
    .Q8_8_Input(A), .BCD2(q8_8_to_decimal_1_bcd2), .BCD1(q8_8_to_decimal_1_bcd1),
    .BCD1_2(q8_8_to_decimal_1_bcd1_2), .Decimal_Point(q8_8_to_decimal_1_decimal_point),
    .BCD1_3(q8_8_to_decimal_1_bcd1_3), .BCD1_4(q8_8_to_decimal_1_bcd1_4), .BCD1_5(q8_8_to_decimal_1_bcd1_5),
    .BCD1_6(q8_8_to_decimal_1_bcd1_6));
  Hex_Digit_Display hex_digit_display_5 (.value(q8_8_to_decimal_2_bcd1));  // open: dp
  Hex_Digit_Display hex_digit_display_6 (.value(q8_8_to_decimal_2_bcd1_2), .dp(q8_8_to_decimal_2_decimal_point));
  Q8_8_to_Decimal q8_8_to_decimal_2 (
    .Q8_8_Input(B), .BCD2(q8_8_to_decimal_2_bcd2), .BCD1(q8_8_to_decimal_2_bcd1),
    .BCD1_2(q8_8_to_decimal_2_bcd1_2), .Decimal_Point(q8_8_to_decimal_2_decimal_point),
    .BCD1_3(q8_8_to_decimal_2_bcd1_3), .BCD1_4(q8_8_to_decimal_2_bcd1_4), .BCD1_5(q8_8_to_decimal_2_bcd1_5),
    .BCD1_6(q8_8_to_decimal_2_bcd1_6));
  Hex_Digit_Display hex_digit_display_7 (.value(q8_8_to_decimal_1_bcd1_3));  // open: dp
  Hex_Digit_Display hex_digit_display_8 (.value(q8_8_to_decimal_1_bcd1_4));  // open: dp
  Hex_Digit_Display hex_digit_display_9 (.value(q8_8_to_decimal_2_bcd1_4));  // open: dp
  Hex_Digit_Display hex_digit_display_10 (.value(q8_8_to_decimal_2_bcd1_3));  // open: dp
  Hex_Digit_Display hex_digit_display_11 (.value(q8_8_to_decimal_1_bcd1_6));  // open: dp
  Hex_Digit_Display hex_digit_display_12 (.value(q8_8_to_decimal_1_bcd1_5));  // open: dp
  Hex_Digit_Display hex_digit_display_13 (.value(q8_8_to_decimal_2_bcd1_6));  // open: dp
  Hex_Digit_Display hex_digit_display_14 (.value(q8_8_to_decimal_2_bcd1_5));  // open: dp
  Example example_1 (
    .A(A), .example_instruction(example_instruction), .Clock(clock_1_out), .Result(example_1_result),
    .example_ready(Example_Ready));
  Division division_1 (
    .Dividend(A), .Divisor(B), .division_instruction(division_instruction), .Clock(clock_1_out),
    .Quotient(division_1_quotient), .division_ready(Division_Ready));
  Square_Root square_root_1 (
    .Q8_8_Input(A), .square_root_instruction(square_root_instruction), .Clock(clock_1_out),
    .Solution(square_root_1_solution), .square_root_ready(Square_Root_Ready));
  Clock clock_1 (.out(clock_1_out));
  Hex_Digit_Display hex_digit_display_15 (.value(q8_8_to_decimal_3_bcd1));  // open: dp
  Hex_Digit_Display hex_digit_display_16 (.value(q8_8_to_decimal_3_bcd2));  // open: dp
  Hex_Digit_Display hex_digit_display_17 (.value(q8_8_to_decimal_4_bcd1));  // open: dp
  Hex_Digit_Display hex_digit_display_18 (.value(q8_8_to_decimal_4_bcd2));  // open: dp
  Hex_Digit_Display hex_digit_display_19 (.value(q8_8_to_decimal_5_bcd2));  // open: dp
  Hex_Digit_Display hex_digit_display_20 (.value(q8_8_to_decimal_5_bcd1));  // open: dp
  Hex_Digit_Display hex_digit_display_21 (.value(q8_8_to_decimal_3_bcd1_3));  // open: dp
  Hex_Digit_Display hex_digit_display_22 (.value(q8_8_to_decimal_3_bcd1_2), .dp(q8_8_to_decimal_3_decimal_point));
  Q8_8_to_Decimal q8_8_to_decimal_3 (
    .Q8_8_Input(example_1_result), .BCD2(q8_8_to_decimal_3_bcd2), .BCD1(q8_8_to_decimal_3_bcd1),
    .BCD1_2(q8_8_to_decimal_3_bcd1_2), .Decimal_Point(q8_8_to_decimal_3_decimal_point),
    .BCD1_3(q8_8_to_decimal_3_bcd1_3), .BCD1_4(q8_8_to_decimal_3_bcd1_4), .BCD1_5(q8_8_to_decimal_3_bcd1_5),
    .BCD1_6(q8_8_to_decimal_3_bcd1_6));
  Hex_Digit_Display hex_digit_display_23 (.value(q8_8_to_decimal_4_bcd1_3));  // open: dp
  Hex_Digit_Display hex_digit_display_24 (.value(q8_8_to_decimal_4_bcd1_2), .dp(q8_8_to_decimal_4_decimal_point));
  Q8_8_to_Decimal q8_8_to_decimal_4 (
    .Q8_8_Input(division_1_quotient), .BCD2(q8_8_to_decimal_4_bcd2), .BCD1(q8_8_to_decimal_4_bcd1),
    .BCD1_2(q8_8_to_decimal_4_bcd1_2), .Decimal_Point(q8_8_to_decimal_4_decimal_point),
    .BCD1_3(q8_8_to_decimal_4_bcd1_3), .BCD1_4(q8_8_to_decimal_4_bcd1_4), .BCD1_5(q8_8_to_decimal_4_bcd1_5),
    .BCD1_6(q8_8_to_decimal_4_bcd1_6));
  Hex_Digit_Display hex_digit_display_25 (.value(q8_8_to_decimal_5_bcd1_2), .dp(q8_8_to_decimal_5_decimal_point));
  Hex_Digit_Display hex_digit_display_26 (.value(q8_8_to_decimal_5_bcd1_3));  // open: dp
  Q8_8_to_Decimal q8_8_to_decimal_5 (
    .Q8_8_Input(square_root_1_solution), .BCD2(q8_8_to_decimal_5_bcd2), .BCD1(q8_8_to_decimal_5_bcd1),
    .BCD1_2(q8_8_to_decimal_5_bcd1_2), .Decimal_Point(q8_8_to_decimal_5_decimal_point),
    .BCD1_3(q8_8_to_decimal_5_bcd1_3), .BCD1_4(q8_8_to_decimal_5_bcd1_4), .BCD1_5(q8_8_to_decimal_5_bcd1_5),
    .BCD1_6(q8_8_to_decimal_5_bcd1_6));
  Hex_Digit_Display hex_digit_display_27 (.value(q8_8_to_decimal_3_bcd1_4));  // open: dp
  Hex_Digit_Display hex_digit_display_28 (.value(q8_8_to_decimal_3_bcd1_5));  // open: dp
  Hex_Digit_Display hex_digit_display_29 (.value(q8_8_to_decimal_4_bcd1_5));  // open: dp
  Hex_Digit_Display hex_digit_display_30 (.value(q8_8_to_decimal_4_bcd1_4));  // open: dp
  Hex_Digit_Display hex_digit_display_31 (.value(q8_8_to_decimal_5_bcd1_4));  // open: dp
  Hex_Digit_Display hex_digit_display_32 (.value(q8_8_to_decimal_5_bcd1_5));  // open: dp
  Hex_Digit_Display hex_digit_display_33 (.value(q8_8_to_decimal_3_bcd1_6));  // open: dp
  Hex_Digit_Display hex_digit_display_34 (.value(q8_8_to_decimal_4_bcd1_6));  // open: dp
  Hex_Digit_Display hex_digit_display_35 (.value(q8_8_to_decimal_5_bcd1_6));  // open: dp

  // Notes on the sheet:
  //   Outputs 0 when divisor is 0
endmodule

module Q8_8_to_Decimal (
  input  [15:0] Q8_8_Input,
  output Decimal_Point,
  output [3:0] BCD2,
  output [3:0] BCD1,
  output [3:0] BCD1_2,
  output [3:0] BCD1_3,
  output [3:0] BCD1_4,
  output [3:0] BCD1_5,
  output [3:0] BCD1_6
);

  wire [15:0] divider_1_rem, divider_2_rem;
  wire [15:4] divider_1_out, divider_2_out, divider_3_out;
  wire [16:0] adder_1_out, adder_2_out, adder_3_out, adder_4_out, adder_5_out, adder_6_out, adder_7_out,
       divider_4_rem, divider_5_out, divider_6_rem, multiplexer_1_out, multiplexer_2_out, multiplexer_3_out,
       multiplexer_4_out, multiplexer_5_out, multiplexer_6_out, multiplexer_7_out, multiplexer_8_out;
  wire [16:4] divider_4_out, divider_6_out, divider_7_out, divider_7_rem;

  Divider #(.width(16)) divider_1 (
    .a(Q8_8_Input), .b(16'h6400), .out({divider_1_out, BCD2}), .rem(divider_1_rem));  // open: upper
  Divider #(.width(16)) divider_2 (
    .a(divider_1_rem), .b(16'ha00), .out({divider_2_out, BCD1}), .rem(divider_2_rem));  // open: upper
  Multiplexer #(.width(17), .enable("false")) multiplexer_1 (
    .in0({17{1'b0}}), .in1(17'hc350), .out(multiplexer_1_out), .sel(Q8_8_Input[7]));
  Multiplexer #(.width(17), .enable("false")) multiplexer_2 (
    .in0({17{1'b0}}), .in1(17'h61a8), .out(multiplexer_2_out), .sel(Q8_8_Input[6]));
  Multiplexer #(.width(17), .enable("false")) multiplexer_3 (
    .in0({17{1'b0}}), .in1(17'h30d4), .out(multiplexer_3_out), .sel(Q8_8_Input[5]));
  Multiplexer #(.width(17), .enable("false")) multiplexer_4 (
    .in0({17{1'b0}}), .in1(17'h186a), .out(multiplexer_4_out), .sel(Q8_8_Input[4]));
  Multiplexer #(.width(17), .enable("false")) multiplexer_5 (
    .in0({17{1'b0}}), .in1(17'hc35), .out(multiplexer_5_out), .sel(Q8_8_Input[3]));
  Multiplexer #(.width(17), .enable("false")) multiplexer_6 (
    .in0({17{1'b0}}), .in1(17'h61b), .out(multiplexer_6_out), .sel(Q8_8_Input[2]));
  Multiplexer #(.width(17), .enable("false")) multiplexer_7 (
    .in0({17{1'b0}}), .in1(17'h30d), .out(multiplexer_7_out), .sel(Q8_8_Input[1]));
  Multiplexer #(.width(17), .enable("false")) multiplexer_8 (
    .in0({17{1'b0}}), .in1(17'h187), .out(multiplexer_8_out), .sel(Q8_8_Input[0]));
  Divider #(.width(16)) divider_3 (.a(divider_2_rem), .b(16'h100), .out({divider_3_out, BCD1_2}));  // open: upper, rem
  Adder #(.width(17)) adder_1 (.a(multiplexer_1_out), .b(multiplexer_2_out), .out(adder_1_out));  // open: cin, cout
  Adder #(.width(17)) adder_2 (.a(multiplexer_3_out), .b(multiplexer_4_out), .out(adder_2_out));  // open: cin, cout
  Adder #(.width(17)) adder_3 (.a(multiplexer_5_out), .b(multiplexer_6_out), .out(adder_3_out));  // open: cin, cout
  Adder #(.width(17)) adder_4 (.a(multiplexer_7_out), .b(multiplexer_8_out), .out(adder_4_out));  // open: cin, cout
  Adder #(.width(17)) adder_5 (.a(adder_1_out), .b(adder_2_out), .out(adder_5_out));  // open: cin, cout
  Adder #(.width(17)) adder_6 (.a(adder_5_out), .b(adder_7_out), .out(adder_6_out));  // open: cin, cout
  Adder #(.width(17)) adder_7 (.a(adder_3_out), .b(adder_4_out), .out(adder_7_out));  // open: cin, cout
  Divider #(.width(17)) divider_4 (
    .a(divider_5_out), .b(17'h3e8), .out({divider_4_out, BCD1_3}), .rem(divider_4_rem));  // open: upper
  Divider #(.width(17)) divider_5 (.a(adder_6_out), .b(17'ha), .out(divider_5_out));  // open: upper, rem
  Divider #(.width(17)) divider_6 (
    .a(divider_4_rem), .b(17'h64), .out({divider_6_out, BCD1_4}), .rem(divider_6_rem));  // open: upper
  Divider #(.width(17)) divider_7 (
    .a(divider_6_rem), .b(17'ha), .out({divider_7_out, BCD1_5}), .rem({divider_7_rem, BCD1_6}));  // open: upper

  assign Decimal_Point = 1'b1;
endmodule

module Example (
  input  [15:0] A,
  input  example_instruction,
  input  Clock,
  output [15:0] Result,
  output example_ready
);

  wire and_1_out, not_1_out;
  wire [7:0] counter_1_q, rom_1_data;
  wire [15:0] adder_1_out, multiplexer_1_out, shifter_1_out, subtractor_1_out;

  not not_1 (not_1_out, example_instruction);
  Multiplexer #(.width(16)) multiplexer_1 (
    .in0(A), .in1(subtractor_1_out), .out(multiplexer_1_out), .sel(rom_1_data[0]));  // open: en
  Counter #(.max('h4), .ongoal("stay"), .trigger("falling")) counter_1 (
    .Q(counter_1_q), .carry(example_ready), .clk(and_1_out), .clr(not_1_out));  // open: load, D, count
  and and_1 (and_1_out, example_instruction, Clock);
  Register #(.width(16), .trigger("falling")) u_result (
    .D(multiplexer_1_out), .en(rom_1_data[1]), .Q(Result), .clk(and_1_out));  // open: clr
  ROM rom_1 (.addr(counter_1_q), .data(rom_1_data));  // open: sel
  Shifter #(.width(16)) shifter_1 (.in(Result), .\dist (4'b0001), .out(shifter_1_out));
  Adder #(.width(16)) adder_1 (.a(shifter_1_out), .b(16'h100), .out(adder_1_out));  // open: cin, cout
  Subtractor #(.width(16)) subtractor_1 (.a(adder_1_out), .b(Result), .out(subtractor_1_out));  // open: bin, bout

  // Notes on the sheet:
  //   result = A;
  //   Given an input A in Q8.8 Format,
  //   In other words, it perform the following:
  //   result = (2 * result + 1.0) - result;
  //   result = (2 * result + 1.0) - result;
  //   this circuit produces a result according to the following equation:
  //   result = (2 * ((2 * A + 1.0) - A) + 1.0) - A
  //   Clock for internal registers
endmodule

module Division (
  input  [15:0] Dividend,
  input  [15:0] Divisor,
  input  division_instruction,
  input  Clock,
  output [15:0] Quotient,
  output division_ready
);

  wire and_1_out, and_2_out, and_3_out, and_4_out, not_1_out, not_2_out, or_1_out, remainder_test_1_less_than;
  wire [7:0] counter_1_q, rom_1_data;
  wire [15:0] Dividend_q, multiplexer_4_out, Quotient_q, shifter_3_out, Temp_q,
       update_quotient_1_new_quotient;
  wire [31:0] Divisor_q, multiplexer_1_out, multiplexer_2_out, multiplexer_3_out, multiplexer_5_out,
       Remainder_q, shifter_1_out, shifter_2_out, shifter_4_out, subtractor_1_out,
       update_divisor_1_sign_extended_value, update_divisor_2_sign_extended_value;

  update_divisor update_divisor_1 (.Divisor(Divisor), .Sign_extended_value(update_divisor_1_sign_extended_value));
  Shifter #(.width(32)) shifter_1 (.in(update_divisor_1_sign_extended_value), .\dist (5'b10000), .out(shifter_1_out));
  Multiplexer #(.width(32)) multiplexer_1 (
    .in0(shifter_2_out), .in1(shifter_1_out), .out(multiplexer_1_out), .sel(rom_1_data[0]));  // open: en
  Register #(.width(16), .trigger("falling")) u_Dividend (
    .D(Dividend), .Q(Dividend_q), .clk(and_1_out));  // open: en, clr
  Register #(.width(32), .trigger("falling")) u_Divisor (
    .D(multiplexer_1_out), .Q(Divisor_q), .clk(and_1_out));  // open: en, clr
  not not_1 (not_1_out, division_instruction);
  or or_1 (or_1_out, Divisor[0], Divisor[1], Divisor[2], Divisor[3], Divisor[4], Divisor[5], Divisor[6], Divisor[7], Divisor[8], Divisor[9], Divisor[10], Divisor[11], Divisor[12], Divisor[13], Divisor[14], Divisor[15]);
  update_divisor update_divisor_2 (.Divisor(Dividend_q), .Sign_extended_value(update_divisor_2_sign_extended_value));
  Shifter #(.width(32), .shift("lr")) shifter_2 (.in(Divisor_q), .\dist (5'b00001), .out(shifter_2_out));
  Counter #(.max('h26), .ongoal("stay"), .trigger("falling")) counter_1 (
    .Q(counter_1_q), .carry(division_ready), .clk(and_1_out), .clr(not_1_out));  // open: load, D, count
  and and_1 (and_1_out, division_instruction, Clock);
  ROM rom_1 (.addr(counter_1_q), .data(rom_1_data));  // open: sel
  Subtractor #(.width(32)) subtractor_1 (.a(Remainder_q), .b(Divisor_q), .out(subtractor_1_out));  // open: bin, bout
  Multiplexer #(.width(32)) multiplexer_2 (
    .in0(multiplexer_3_out), .in1(update_divisor_2_sign_extended_value), .out(multiplexer_2_out),
    .sel(rom_1_data[0]));  // open: en
  remainder_test remainder_test_1 (.Remainder(subtractor_1_out), .Less_Than(remainder_test_1_less_than));
  Multiplexer #(.width(32)) multiplexer_3 (
    .in0(subtractor_1_out), .in1(Remainder_q), .out(multiplexer_3_out), .sel(remainder_test_1_less_than));  // open: en
  update_quotient update_quotient_1 (
    .Quotient(Quotient_q), .New_Quotient(update_quotient_1_new_quotient),
    .less_than(remainder_test_1_less_than));
  Multiplexer #(.width(16)) multiplexer_4 (
    .in0({16{1'b0}}), .in1(update_quotient_1_new_quotient), .out(multiplexer_4_out), .sel(rom_1_data[1]));  // open: en
  not not_2 (not_2_out, division_ready);
  Multiplexer #(.width(32)) multiplexer_5 (
    .in0(multiplexer_2_out), .in1(shifter_4_out), .out(multiplexer_5_out), .sel(and_3_out));  // open: en
  and and_2 (and_2_out, not_2_out, and_1_out);
  and and_3 (and_3_out, rom_1_data[2], Clock);
  Register #(.width(32), .trigger("falling")) Remainder (
    .D(multiplexer_5_out), .en(rom_1_data[4]), .Q(Remainder_q), .clk(and_2_out));  // open: clr
  Register #(.width(16), .trigger("falling")) u_Quotient (
    .D(multiplexer_4_out), .en(and_4_out), .Q(Quotient_q), .clk(and_2_out));  // open: clr
  and and_4 (and_4_out, rom_1_data[1], or_1_out);
  Shifter #(.width(16)) shifter_3 (.in(Quotient_q), .\dist (4'b1000), .out(shifter_3_out));
  Shifter #(.width(32)) shifter_4 (.in(Remainder_q), .\dist (5'b01000), .out(shifter_4_out));
  final_quotient final_quotient_1 (.first_restult(Temp_q), .Second_result(Quotient_q), .Quotient(Quotient));
  Register #(.width(16), .trigger("falling")) Temp (
    .D(shifter_3_out), .en(rom_1_data[3]), .Q(Temp_q), .clk(and_3_out));  // open: clr

  // Notes on the sheet:
  //   shift divisor left 16
  //   extend dividend to 32 bits
  //   contents of rom_1 (hex, n*v repeats v):
  //   1 11 17*12 1d 5 17*12
  //   Clock for internal registers
  //   needed for when divisor is 0
  //   subtract divisor from remainder
endmodule

module Square_Root (
  input  [15:0] Q8_8_Input,
  input  square_root_instruction,
  input  Clock,
  output [15:0] Solution,
  output square_root_ready
);

  wire and_1_out, and_2_out, not_1_out, not_2_out, not_3_out, not_4_out, or_1_out, setless_1_less_than,
       zero_1_output;
  wire [4:0] adder_1_out, counter_1_q, shifter_1_out;
  wire [7:0] counter_2_q, rom_1_data;
  wire [31:0] adder_2_out, adder_3_out, multiplexer_1_out, multiplexer_2_out, multiplexer_3_out,
       multiplexer_4_out, Multiplier_q, Quotient_q, Result_q, shift_add1_1_output, shifter_2_out,
       shifter_3_out, shifter_4_out, shifter_5_out, shifter_6_out, shifter_7_out, shifter_8_out,
       squpdate_1_output, subtractor_1_out, subtractor_2_out, subtractor_3_out,
       update_divisor_1_sign_extended_value, Value_q;

  Multiplexer #(.width(32)) multiplexer_1 (
    .in0({32{1'b0}}), .in1(multiplexer_2_out), .out(multiplexer_1_out), .sel(rom_1_data[0]));  // open: en
  update_divisor update_divisor_1 (.Divisor(Q8_8_Input), .Sign_extended_value(update_divisor_1_sign_extended_value));
  not not_1 (not_1_out, square_root_instruction);
  Counter #(.width(5), .max('h10), .ongoal("stay"), .trigger("falling")) counter_1 (
    .Q(counter_1_q), .clk(and_1_out), .clr(not_1_out));  // open: load, D, count, carry
  Register #(.width(32), .trigger("falling")) Value (
    .D(update_divisor_1_sign_extended_value), .Q(Value_q), .clk(and_1_out), .clr(not_1_out));  // open: en
  Adder #(.width(5)) adder_1 (.a(5'b01110), .b(shifter_1_out), .out(adder_1_out));  // open: cin, cout
  Shifter #(.width(5)) shifter_1 (.in(counter_1_q), .\dist (3'b001), .out(shifter_1_out));
  Adder #(.width(32)) adder_2 (.a(multiplexer_1_out), .b(32'h1), .out(adder_2_out));  // open: cin, cout
  Counter #(.max('hd), .ongoal("stay"), .trigger("falling")) counter_2 (
    .Q(counter_2_q), .carry(square_root_ready), .clk(and_1_out), .clr(not_2_out));  // open: load, D, count
  not not_2 (not_2_out, square_root_instruction);
  and and_1 (and_1_out, square_root_instruction, Clock);
  Register #(.width(32), .trigger("falling")) Multiplier (
    .D(adder_2_out), .Q(Multiplier_q), .clk(and_1_out), .clr(not_1_out));  // open: en
  ROM rom_1 (.addr(counter_2_q), .data(rom_1_data));  // open: sel
  Shifter #(.width(32)) shifter_2 (.in(Value_q), .\dist (adder_1_out), .out(shifter_2_out));
  Adder #(.width(32)) adder_3 (.a(Multiplier_q), .b(32'h1), .out(adder_3_out));  // open: cin, cout
  Shifter #(.width(32)) shifter_3 (.in(adder_3_out), .\dist (5'b00001), .out(shifter_3_out));
  SqUpdate squpdate_1 (.Two_Bits(shifter_4_out), .SrVal(Quotient_q), .\output (squpdate_1_output));
  Shifter #(.width(32), .shift("lr")) shifter_4 (.in(shifter_2_out), .\dist (5'b11110), .out(shifter_4_out));
  Subtractor #(.width(32)) subtractor_1 (.a(Multiplier_q), .b(32'h1), .out(subtractor_1_out));  // open: bin, bout
  Subtractor #(.width(32)) subtractor_2 (
    .a(Multiplier_q), .b(squpdate_1_output), .out(subtractor_2_out));  // open: bin, bout
  Shifter #(.width(32)) shifter_5 (.in(subtractor_1_out), .\dist (5'b00001), .out(shifter_5_out));
  Shifter #(.width(32)) shifter_6 (.in(squpdate_1_output), .\dist (5'b00010), .out(shifter_6_out));
  Subtractor #(.width(32)) subtractor_3 (
    .a(squpdate_1_output), .b(Multiplier_q), .out(subtractor_3_out));  // open: bin, bout
  Zero zero_1 (.square_root(subtractor_2_out), .Output(zero_1_output));
  not not_3 (not_3_out, zero_1_output);
  setLess setless_1 (.Divisor(subtractor_2_out), .less_than(setless_1_less_than));
  Multiplexer #(.width(32)) multiplexer_2 (
    .in0(shifter_5_out), .in1(shifter_3_out), .out(multiplexer_2_out), .sel(or_1_out));  // open: en
  or or_1 (or_1_out, not_3_out, setless_1_less_than);
  Multiplexer #(.width(32)) multiplexer_3 (
    .in0(shifter_7_out), .in1(shift_add1_1_output), .out(multiplexer_3_out), .sel(or_1_out));  // open: en
  Shift_add1 shift_add1_1 (.Value(Result_q), .\output (shift_add1_1_output));
  Shifter #(.width(32)) shifter_7 (.in(Result_q), .\dist (5'b00001), .out(shifter_7_out));
  Shifter #(.width(32)) shifter_8 (.in(subtractor_3_out), .\dist (5'b00010), .out(shifter_8_out));
  and and_2 (and_2_out, or_1_out, and_1_out);
  Register #(.width(32), .trigger("falling")) Result (
    .D(multiplexer_3_out), .en(rom_1_data[0]), .Q(Result_q), .clk(and_1_out), .clr(not_4_out));
  Multiplexer #(.width(32)) multiplexer_4 (
    .in0(shifter_6_out), .in1(shifter_8_out), .out(multiplexer_4_out), .sel(and_2_out));  // open: en
  shrink_sr shrink_sr_1 (.Answer(Result_q), ._16_bit(Solution));
  Register #(.width(32), .trigger("falling")) Quotient (
    .D(multiplexer_4_out), .Q(Quotient_q), .clk(and_1_out), .clr(not_4_out));  // open: en
  not not_4 (not_4_out, square_root_instruction);

  // Notes on the sheet:
  //   shift left
  //   contents of rom_1 (hex, n*v repeats v):
  //   0 12*1
  //   Clock for internal registers
  //   if mult and sq equal
  //   shirt right to get first 2 bits
  //   check less than
endmodule

module remainder_test (
  input  [31:0] Remainder,
  output Less_Than
);


  assign Less_Than = Remainder[31];
endmodule

module update_quotient (
  input  less_than,
  input  [15:0] Quotient,
  output [15:0] New_Quotient
);

  wire [15:0] adder_1_out, shifter_1_out;

  Shifter #(.width(16)) shifter_1 (.in(Quotient), .\dist (4'b0001), .out(shifter_1_out));
  Adder #(.width(16)) adder_1 (.a(shifter_1_out), .b(16'h1), .out(adder_1_out));  // open: cin, cout
  Multiplexer #(.width(16)) multiplexer_1 (
    .in0(adder_1_out), .in1(shifter_1_out), .out(New_Quotient), .sel(less_than));  // open: en
endmodule

module update_divisor (
  input  [15:0] Divisor,
  output [31:0] Sign_extended_value
);


  assign Sign_extended_value = {{16{1'b0}}, Divisor};
endmodule

module final_quotient (
  input  [15:0] first_restult,
  input  [15:0] Second_result,
  output [15:0] Quotient
);


  assign Quotient = {first_restult[15:8], Second_result[7:0]};
endmodule

module Zero (
  input  [31:0] square_root,
  output Output
);

  or or_1 (Output, square_root[0], square_root[1], square_root[2], square_root[3], square_root[4], square_root[5], square_root[6], square_root[7], square_root[8], square_root[9], square_root[10], square_root[11], square_root[12], square_root[13], square_root[14], square_root[15], square_root[16], square_root[17], square_root[18], square_root[19], square_root[20], square_root[21], square_root[22], square_root[23], square_root[24], square_root[25], square_root[26], square_root[27], square_root[28], square_root[29], square_root[30], square_root[31]);
endmodule

module Shift_add1 (
  input  [31:0] Value,
  output [31:0] \output 
);

  wire [31:0] shifter_1_out;

  Shifter #(.width(32)) shifter_1 (.in(Value), .\dist (5'b00001), .out(shifter_1_out));
  Adder #(.width(32)) adder_1 (.a(shifter_1_out), .b(32'h1), .out(\output ));  // open: cin, cout
endmodule

module setLess (
  input  [31:0] Divisor,
  output less_than
);

  and and_1 (less_than, Divisor[31], 1'b1);
endmodule

module SqUpdate (
  input  [31:0] Two_Bits,
  input  [31:0] SrVal,
  output [31:0] \output 
);

  assign \output  = Two_Bits | SrVal;  // OR_Gate or_1, 32 bits wide
endmodule

module shrink_sr (
  input  [31:0] Answer,
  output [15:0] _16_bit
);


  assign _16_bit = Answer[15:0];
endmodule
